// Logisim project NewCPU.circ as structural Verilog: 8 circuits, main circuit main
module main (
);

  wire [7:0] program_counter_1_p1;

  // Program_counter program_counter_1: pin names not known; wires that end beside it: program_counter_1_p1
  RAM_Simulator ram_simulator_1 (.D_OUT(program_counter_1_p1));  // open: Addr, D_IN
endmodule

module full_adder_1_bit (
  input  A,
  input  B,
  input  CIN,
  output SUM,
  output COUT
);

  wire n7408_1_pin3, n7408_1_pin11, n7486_1_pin6;

  _7486 #(.ShowInternalStructure("true")) u_7486_1 (
    .pin4(A), .pin5(B), .pin6(n7486_1_pin6), .pin10(n7486_1_pin6), .pin9(CIN), .pin8(SUM));  // open: pin1, pin2, pin3, pin13, pin12, pin11
  _7408 #(.ShowInternalStructure("true")) u_7408_1 (
    .pin1(A), .pin2(B), .pin3(n7408_1_pin3), .pin13(n7486_1_pin6), .pin12(CIN), .pin11(n7408_1_pin11));  // open: pin4, pin5, pin6, pin10, pin9, pin8
  _7432 #(.ShowInternalStructure("true")) u_7432_1 (
    .pin13(n7408_1_pin11), .pin12(n7408_1_pin3), .pin11(COUT));  // open: pin1, pin2, pin3, pin4, pin5, pin6, pin10, pin9, pin8
  // _74181 74181_1: pin names not known
endmodule

module Program_counter (
  input  Clear,
  input  Clock,
  output [3:0] CountOut
);

  wire n74161_1_pin3, n74161_1_pin7;

  _74161 #(.ShowInternalStructure("true")) u_74161_1 (
    .pin1(Clear), .pin2(Clock), .pin3(n74161_1_pin3), .pin4(n74161_1_pin3), .pin5(n74161_1_pin3),
    .pin6(n74161_1_pin3), .pin7(n74161_1_pin7), .pin14(CountOut[0]), .pin13(CountOut[1]),
    .pin12(CountOut[2]), .pin11(CountOut[3]), .pin10(n74161_1_pin7), .pin9(n74161_1_pin7));  // open: pin15
  // also tied to GND on the sheet: n74161_1_pin3
  // also tied to VCC on the sheet: n74161_1_pin7
endmodule

module RAM_Simulator (
  input  [3:0] Addr,
  input  [7:0] D_IN,
  output [7:0] D_OUT
);


  assign D_OUT = D_IN;
endmodule

module instruction_reg (
  input  [7:0] IR_IN,
  input  CLR,
  input  CLK,
  output [3:0] IMM,
  output [2:0] OP
);

  wire n74175_2_pin2;
  wire [0:0] pull_resistor_1_node;

  Pull_Resistor pull_resistor_1 (.node(pull_resistor_1_node[0]));
  _74175 #(.ShowInternalStructure("true")) u_74175_1 (
    .pin1(CLR), .pin2(IMM[3]), .pin4(IR_IN[4]), .pin5(IR_IN[3]), .pin7(IMM[2]), .pin15(IMM[0]),
    .pin13(IR_IN[1]), .pin12(IR_IN[2]), .pin10(IMM[1]), .pin9(CLK));  // open: pin3, pin6, pin14, pin11
  _74175 #(.ShowInternalStructure("true")) u_74175_2 (
    .pin1(CLR), .pin2(n74175_2_pin2), .pin4(pull_resistor_1_node[0]), .pin5(IR_IN[7]), .pin7(OP[2]),
    .pin15(OP[0]), .pin13(IR_IN[5]), .pin12(IR_IN[6]), .pin10(OP[1]), .pin9(CLK));  // open: pin3, pin6, pin14, pin11
endmodule

module reg_a (
  input  nCLR,
  input  [3:0] D,
  input  LOAD,
  input  CLK,
  output [3:0] Q
);

  wire n74175_1_pin9;

  _74175 #(.ShowInternalStructure("true")) u_74175_1 (
    .pin1(nCLR), .pin2(Q[0]), .pin4(D[0]), .pin5(D[1]), .pin7(Q[1]), .pin15(Q[3]), .pin13(D[3]),
    .pin12(D[2]), .pin10(Q[2]), .pin9(n74175_1_pin9));  // open: pin3, pin6, pin14, pin11
  _7408 #(.ShowInternalStructure("true")) u_7408_1 (
    .pin1(LOAD), .pin2(CLK), .pin3(n74175_1_pin9));  // open: pin4, pin5, pin6, pin13, pin12, pin11, pin10, pin9, pin8
endmodule

module reg_b (
  input  nCLR,
  input  [3:0] D,
  input  LOAD,
  input  CLK,
  output [3:0] Q
);

  wire n74175_1_pin9;

  _74175 #(.ShowInternalStructure("true")) u_74175_1 (
    .pin1(nCLR), .pin2(Q[0]), .pin4(D[0]), .pin5(D[1]), .pin7(Q[1]), .pin15(Q[3]), .pin13(D[3]),
    .pin12(D[2]), .pin10(Q[2]), .pin9(n74175_1_pin9));  // open: pin3, pin6, pin14, pin11
  _7408 #(.ShowInternalStructure("true")) u_7408_1 (
    .pin1(LOAD), .pin2(CLK), .pin3(n74175_1_pin9));  // open: pin4, pin5, pin6, pin13, pin12, pin11, pin10, pin9, pin8
endmodule

module alu (
  input  [3:0] A,
  input  [3:0] B,
  input  SUB,
  input  [2:0] OP,
  output [3:0] RESULT
);

  wire full_adder_1_bit_1_cout, full_adder_1_bit_2_cout, full_adder_1_bit_3_cout, n7486_1_pin3, n7486_1_pin6,
       n7486_1_pin8, n7486_1_pin11, n74157_1_pin4, n74157_1_pin7, n74157_1_pin9, n74157_1_pin12;
  wire [3:0] AndOut, OROut, SumOut;

  _7486 u_7486_1 (
    .pin1(B[0]), .pin2(SUB), .pin3(n7486_1_pin3), .pin4(B[1]), .pin5(SUB), .pin6(n7486_1_pin6), .pin13(B[2]),
    .pin12(SUB), .pin11(n7486_1_pin11), .pin10(B[3]), .pin9(SUB), .pin8(n7486_1_pin8));
  _7408 u_7408_1 (
    .pin1(A[0]), .pin2(B[0]), .pin3(AndOut[0]), .pin4(A[1]), .pin5(B[1]), .pin6(AndOut[1]), .pin13(A[2]),
    .pin12(B[2]), .pin11(AndOut[2]), .pin10(A[3]), .pin9(B[3]), .pin8(AndOut[3]));
  _7432 u_7432_1 (
    .pin1(A[0]), .pin2(B[0]), .pin3(OROut[0]), .pin4(A[1]), .pin5(B[1]), .pin6(OROut[1]), .pin13(A[2]),
    .pin12(B[2]), .pin11(OROut[2]), .pin10(A[3]), .pin9(B[3]), .pin8(OROut[3]));
  full_adder_1_bit full_adder_1_bit_1 (
    .A(A[0]), .B(n7486_1_pin3), .CIN(SUB), .SUM(SumOut[0]), .COUT(full_adder_1_bit_1_cout));
  full_adder_1_bit full_adder_1_bit_2 (
    .A(A[1]), .B(n7486_1_pin6), .CIN(full_adder_1_bit_1_cout), .SUM(SumOut[1]), .COUT(full_adder_1_bit_2_cout));
  full_adder_1_bit full_adder_1_bit_3 (
    .A(A[2]), .B(n7486_1_pin11), .CIN(full_adder_1_bit_2_cout), .SUM(SumOut[2]),
    .COUT(full_adder_1_bit_3_cout));
  full_adder_1_bit full_adder_1_bit_4 (
    .A(A[3]), .B(n7486_1_pin8), .CIN(full_adder_1_bit_3_cout), .SUM(SumOut[3]));  // open: COUT
  _74157 #(.ShowInternalStructure("true")) u_74157_1 (
    .pin1(OP[1]), .pin2(SumOut[0]), .pin3(AndOut[0]), .pin4(n74157_1_pin4), .pin5(SumOut[1]),
    .pin6(AndOut[1]), .pin7(n74157_1_pin7), .pin14(SumOut[3]), .pin13(AndOut[3]), .pin12(n74157_1_pin12),
    .pin11(SumOut[2]), .pin10(AndOut[2]), .pin9(n74157_1_pin9));  // open: pin15
  _74157 #(.ShowInternalStructure("true")) u_74157_2 (
    .pin1(OP[0]), .pin2(n74157_1_pin4), .pin3(OROut[0]), .pin4(RESULT[0]), .pin5(n74157_1_pin7),
    .pin6(OROut[1]), .pin7(RESULT[1]), .pin14(n74157_1_pin12), .pin13(OROut[3]), .pin12(RESULT[3]),
    .pin11(n74157_1_pin9), .pin10(OROut[2]), .pin9(RESULT[2]));  // open: pin15
endmodule
